# Fritzing sketch Schematic (saved by Fritzing 0.9.0b)

parts:
  Part1 = Arduino Uno (Rev3)  # not connected
  Part2 = Arduino ProtoShield
  Part3 = EasyDriver_v44  # not connected
  M1 = Stepper Motor - Unipolar  # not connected
  LCD1 = LCD screen  # not connected
  Part4 = Thumb Joystick
  J1 = Power Jack [package=power_jack_pth_lock]  # not connected
  U1 = 3.5mm Audio Jack [package=audio-jack-3.5mm-smd]  # not connected
  U2 = 3.5mm Audio Jack [package=audio-jack-3.5mm-smd]  # not connected
  U3 = 3.5mm Audio Jack [package=audio-jack-3.5mm-smd]  # not connected
  U4 = 3.5mm Audio Jack [package=audio-jack-3.5mm-smd]  # not connected

nets:
  N1: Part2.A1, Part4.HORZ
  N2: Part2.A0, Part4.VERT
  5V: Part2.5V, Part4.SEL, Part4.VCC
  GND: Part2.GND, Part4.GND
